# Fritzing sketch EnergyMeter (saved by Fritzing 0.9.1b)
circuit board: 3.86cm x 2.8cm
breadboards: 1

parts:
  R1 = Resistor [tolerance=±5% resistance=150k package=THT]
  JP1 = Header 3 [package=molex-1x3_lock]
  BPW40 = LTR-301 [package=ltr-301]
  R2 = Resistor [tolerance=±5% resistance=270 package=THT]
  U1 = 555 Timer [package="DIP8 [THT]"]
  LED1 = LED - 3mm [color="Red (633nm)" package="3 mm [THT]"]

nets:
  N1: R1.Pin_0, BPW40.C, U1.Trigger, U1.Threshold
  3.3V: R1.Pin_1, JP1.1, U1.Reset, U1.Vcc_Supply_Voltage
  N2: JP1.2, U1.Output, LED1.anode
  GND: JP1.3, BPW40.E, R2.Pin_0, U1.Ground
  N3: R2.Pin_1, LED1.cathode

notes:
  EnergyMeter
